# Fritzing sketch Moodstat (saved by Fritzing 0.9.5d)
breadboards: 1

parts:
  Gizwits_WiFi_Witty_ESP-12F1 = Gizwits WiFi Witty ESP-12F
  hc-sr1 = hc-sr04
  S2 = Pushbutton [package="[SMD]"]
  S3 = Pushbutton [package="[SMD]"]
  S4 = Pushbutton [package="[SMD]"]

nets:
  N1: Gizwits_WiFi_Witty_ESP-12F1.GPIO12, hc-sr1.Echo
  N2: Gizwits_WiFi_Witty_ESP-12F1.GPIO13, hc-sr1.Trig
  VCC: Gizwits_WiFi_Witty_ESP-12F1.VCC, hc-sr1.VCC
  GND: Gizwits_WiFi_Witty_ESP-12F1.GND, hc-sr1.GND, S2.Pin_3, S3.Pin_3, S3.Pin_4, S4.Pin_3, S4.Pin_4
  N3: Gizwits_WiFi_Witty_ESP-12F1.GPIO15, S2.Pin_1, S2.Pin_2
  N4: Gizwits_WiFi_Witty_ESP-12F1.GPIO2, S3.Pin_2
  N5: Gizwits_WiFi_Witty_ESP-12F1.GPIO0, S4.Pin_2
